# Fritzing sketch Nunchuck sketch (saved by Fritzing 0.9.3b)
breadboards: 1

parts:
  Disp1 = LBT2088AH [part_number=LBT2088AH]  # not connected
  IC1 = MCP23017 I2C I/O Expander

nets:
  N1: IC1.GPB3, IC1.GPB4
  N2: IC1.GPA3, IC1.GPA4

custom parts:
  MCP23017 I2C I/O Expander: The MCP23017 uses two i2c pins (these can be shared with other i2c devices), and in exchange gives you 16 general purpose pins. You can set each of 16 pins to be input, output, input with a pullup or open drain. There's even the ability to get an interrupt via an external pin when any of the inputs change so you don't have to keep polling the chip.
